# Fritzing sketch bluetooth_programmer (saved by Fritzing 0.9.3b)
circuit board: 8.46667cm x 5.64444cm

parts:
  Bauteil2 = Arduino Mega 2560 (Rev3)
  R3 = Resistor [tolerance=±5% resistance=420 package=THT]
  C1 = Ceramic Capacitor [capacitance=100nF voltage=6.3V package="100 mil [THT, multilayer]"]
  R4 = Resistor [tolerance=±5% resistance=3.6k package=THT]
  R5 = Resistor [tolerance=±5% resistance=1.8k package=THT]
  Bauteil1 = Bluetooth HC-05 Macho
  Tx2 = mystery part, 3 pins [chip_label=?]  # not connected
  Rx2 = mystery part, 4 pins [chip_label=?]  # not connected
  R2 = Resistor [tolerance=±5% resistance=22k package=THT]

nets:
  GND: Bauteil2.GND, R4.Pin_1, Bauteil1.GND, R2.Pin_1
  N1: Bauteil2.RESET, C1.1, R2.Pin_0
  5V: Bauteil2.5V, Bauteil1.VCC
  N2: Bauteil2.D0_RX0, R3.Pin_0
  N3: Bauteil2.D1_TX0, R5.Pin_1
  N4: R3.Pin_1, Bauteil1.RXD
  N5: C1.0, Bauteil1.State
  N6: R4.Pin_0, R5.Pin_0, Bauteil1.TXD

notes:
  Ardunio will be resetted with every Bluetooth connection!
  Pulldown thus the Arduino is resetted more easily
  Voltage devider 5V -> 3.3V
  Resistor enabling communication with bluetooth and usb at the same port (but only with one sender) - without this resistor sending using usb wouldn't be possible
  Capacitor to pass only changes in connection state
